# Fritzing sketch quizboard_2_0 (saved by Fritzing 0.9.3b)
circuit board: 1.39778cm x 2.3706cm
circuit board: 8.46667cm x 5.64444cm
circuit board: 1.39778cm x 2.3706cm
breadboards: 4

parts:
  Bauteil1 = Arduino Uno (Rev3)
  R1 = Resistor [tolerance=±5% resistance=220 package=THT]
  R2 = Resistor [tolerance=±5% resistance=220 package=THT]
  R3 = Resistor [tolerance=±5% resistance=220 package=THT]
  R4 = Resistor [tolerance=±5% resistance=220 package=THT]
  R5 = Resistor [tolerance=±5% resistance=220 package=THT]
  R6 = Resistor [tolerance=±5% resistance=220 package=THT]
  R7 = Resistor [tolerance=±5% resistance=220 package=THT]
  R8 = Resistor [tolerance=±5% resistance=220 package=THT]
  S1 = Pushbutton [package=THT]  # not connected
  LED1 = LED - 5mm [color="Green (565nm)" package="5 mm [THT]"]
  Kont_B = rounded female pin header, 4 pins [form="♀ (female rounded)"]
  Kont_C = rounded female pin header, 4 pins [form="♀ (female rounded)"]
  R37 = Resistor [tolerance=±5% resistance=10M package=THT]
  Kont_A = rounded female pin header, 4 pins [form="♀ (female rounded)"]
  R38 = Resistor [tolerance=±5% resistance=10M package=THT]
  Kont_D = rounded female pin header, 4 pins [form="♀ (female rounded)"]
  R39 = Resistor [tolerance=±5% resistance=10M package=THT]
  R40 = Resistor [tolerance=±5% resistance=10M package=THT]
  Sensor_Buchse = female pin header, 4 pins [form="♀ (female)"]
  R20 = Resistor [tolerance=±5% resistance=1M package=THT]
  R19 = Resistor [tolerance=±5% resistance=1M package=THT]
  R18 = Resistor [tolerance=±5% resistance=1M package=THT]
  R17 = Resistor [tolerance=±5% resistance=1M package=THT]
  R32 = Resistor [tolerance=±5% resistance=1M package=THT]
  R36 = Resistor [tolerance=±5% resistance=1M package=THT]
  R34 = Resistor [tolerance=±5% resistance=1M package=THT]
  R35 = Resistor [tolerance=±5% resistance=1M package=THT]
  R31 = Resistor [tolerance=±5% resistance=1M package=THT]
  R30 = Resistor [tolerance=±5% resistance=1M package=THT]
  R33 = Resistor [tolerance=±5% resistance=1M package=THT]
  R25 = Resistor [tolerance=±5% resistance=1M package=THT]
  LED_Shift = 74HC595 [package="DIP16 [THT]"]
  LED_Bus_Plug = male pin header, 5 pins [form="♂ (male)"]
  LED_Bus_Socket = rounded female pin header, 5 pins [form="♀ (female rounded)"]
  LED2 = LED - 5mm [color="Green (565nm)" package="5 mm [THT]"]
  LED3 = LED - 5mm [color="Green (565nm)" package="5 mm [THT]"]
  LED4 = LED - 5mm [color="Green (565nm)" package="5 mm [THT]"]
  LED5 = LED - 5mm [color="Green (565nm)" package="5 mm [THT]"]
  LED6 = LED - 5mm [color="Green (565nm)" package="5 mm [THT]"]
  LED7 = LED - 5mm [color="Green (565nm)" package="5 mm [THT]"]
  LED8 = LED - 5mm [color="Green (565nm)" package="5 mm [THT]"]
  Plug_Shift = 74HC595 [package="DIP16 [THT]"]
  Plug_Bus = female pin header, 8 pins [form="♀ (female)"]
  7_Segment2 = 7 Segment Display
  7Seg_Shift = 74HC595 [package="DIP16 [THT]"]
  R41 = Resistor [tolerance=±5% resistance=220 package=THT]
  R42 = Resistor [tolerance=±5% resistance=220 package=THT]
  R43 = Resistor [tolerance=±5% resistance=220 package=THT]
  R44 = Resistor [tolerance=±5% resistance=220 package=THT]
  R45 = Resistor [tolerance=±5% resistance=220 package=THT]
  R46 = Resistor [tolerance=±5% resistance=220 package=THT]
  R47 = Resistor [tolerance=±5% resistance=220 package=THT]
  R48 = Resistor [tolerance=±5% resistance=220 package=THT]

nets:
  N1: Bauteil1.A0, R37.Pin_1, Kont_A.pin1, Sensor_Buchse.pin4, R17.Pin_0, R33.Pin_1
  N2: Bauteil1.A1, Kont_B.pin1, R38.Pin_1, Sensor_Buchse.pin3, R18.Pin_0, R30.Pin_1
  N3: Bauteil1.A2, Kont_C.pin1, R39.Pin_1, Sensor_Buchse.pin2, R19.Pin_0, R31.Pin_1
  N4: Bauteil1.A3, Kont_D.pin1, R40.Pin_1, Sensor_Buchse.pin1, R20.Pin_0, R32.Pin_1
  N5: Bauteil1.D8, Plug_Shift.ST_CP
  N6: Bauteil1.D9_PWM, Plug_Shift.SH_CP
  N7: Bauteil1.D10_PWM/SS, LED_Bus_Plug.pin5, LED_Bus_Socket.pin5, 7Seg_Shift.DS
  N8: Bauteil1.D11_PWM/MOSI, LED_Shift.ST_CP, LED_Bus_Plug.pin3, LED_Bus_Socket.pin3, 7Seg_Shift.ST_CP
  N9: Bauteil1.D12/MISO, LED_Shift.SH_CP, LED_Bus_Plug.pin2, LED_Bus_Socket.pin2, 7Seg_Shift.SH_CP
  GND: Bauteil1.GND, LED1.anode, R20.Pin_1, R19.Pin_1, R18.Pin_1, R17.Pin_1, LED_Shift.GND, LED_Shift.OE, LED_Bus_Plug.pin4, LED_Bus_Socket.pin4, LED2.anode, LED3.anode, LED4.anode, LED5.anode, LED6.anode, LED7.anode, LED8.anode, Plug_Shift.GND, Plug_Shift.OE, 7Seg_Shift.GND, 7Seg_Shift.OE
  N10: Bauteil1.D7, Plug_Shift.DS
  VCC: Bauteil1.5V, LED_Shift.MR, LED_Shift.VCC, LED_Bus_Plug.pin1, LED_Bus_Socket.pin1, Plug_Shift.MR, Plug_Shift.VCC, 7_Segment2.common_anode, 7Seg_Shift.MR, 7Seg_Shift.VCC
  N11: R1.Pin_0, LED_Shift.Q7
  N12: R1.Pin_1, LED8.cathode
  N13: R2.Pin_0, LED_Shift.Q6
  N14: R2.Pin_1, LED7.cathode
  N15: R3.Pin_0, LED_Shift.Q5
  N16: R3.Pin_1, LED6.cathode
  N17: R4.Pin_0, LED_Shift.Q4
  N18: R4.Pin_1, LED5.cathode
  N19: R5.Pin_0, LED_Shift.Q3
  N20: R5.Pin_1, LED4.cathode
  N21: R6.Pin_0, LED_Shift.Q2
  N22: R6.Pin_1, LED3.cathode
  N23: R7.Pin_0, LED_Shift.Q0
  N24: R7.Pin_1, LED1.cathode
  N25: R8.Pin_0, LED_Shift.Q1
  N26: R8.Pin_1, LED2.cathode
  N27: Kont_B.pin2, R34.Pin_0, R30.Pin_0
  N28: Kont_B.pin3, R34.Pin_1
  N29: Kont_B.pin4, R38.Pin_0
  N30: Kont_C.pin2, R35.Pin_0, R31.Pin_0
  N31: Kont_C.pin3, R35.Pin_1
  N32: Kont_C.pin4, R39.Pin_0
  N33: R37.Pin_0, Kont_A.pin4
  N34: Kont_A.pin2, R33.Pin_0, R25.Pin_0
  N35: Kont_A.pin3, R25.Pin_1
  N36: Kont_D.pin2, R32.Pin_0, R36.Pin_0
  N37: Kont_D.pin3, R36.Pin_1
  N38: Kont_D.pin4, R40.Pin_0
  N39: LED_Shift.DS, 7Seg_Shift.Q7'
  N40: Plug_Shift.Q1, Plug_Bus.pin7
  N41: Plug_Shift.Q2, Plug_Bus.pin6
  N42: Plug_Shift.Q3, Plug_Bus.pin5
  N43: Plug_Shift.Q4, Plug_Bus.pin4
  N44: Plug_Shift.Q5, Plug_Bus.pin3
  N45: Plug_Shift.Q6, Plug_Bus.pin2
  N46: Plug_Shift.Q7, Plug_Bus.pin1
  N47: Plug_Shift.Q0, Plug_Bus.pin8
  N48: 7_Segment2.Segment_E, R45.Pin_1
  N49: 7_Segment2.Segment_D, R46.Pin_1
  N50: 7_Segment2.Segment_C, R48.Pin_1
  N51: 7_Segment2.Segment_DP, R47.Pin_1
  N52: 7_Segment2.Segment_B, R44.Pin_1
  N53: 7_Segment2.Segment_A, R43.Pin_1
  N54: 7_Segment2.Segment_F, R41.Pin_1
  N55: 7_Segment2.Segment_G, R42.Pin_0
  N56: 7Seg_Shift.Q1, R44.Pin_0
  N57: 7Seg_Shift.Q2, R43.Pin_0
  N58: 7Seg_Shift.Q3, R41.Pin_0
  N59: 7Seg_Shift.Q4, R47.Pin_0
  N60: 7Seg_Shift.Q5, R46.Pin_0
  N61: 7Seg_Shift.Q6, R45.Pin_0
  N62: 7Seg_Shift.Q7, R48.Pin_0
  N63: 7Seg_Shift.Q0, R42.Pin_1
